# Fritzing sketch SFT 2024 BREADBOARD (saved by Fritzing 0.9.3b)
breadboards: 1

parts:
  Part1 = Adafruit ESP32 Feather V2
  OLED_I2C1 = OLED 128x64 I2C Monochrome Display
  M1 = MakerFocus MAX30102
  Mod1 = gy-906
  A1 = ENS160 AHT21
  IC1 = AD8232 HeartRate Monitor [part_number=SEN-12650 chip_label=IC package="DIP (Dual Inline) [THT]"]

nets:
  GND: Part1.GND, Part1.SDA, Part1.IO27_A10, OLED_I2C1.SDA, OLED_I2C1.GND, M1.GND, M1.SDA, Mod1.GND, Mod1.SDA, A1.Pin_3, A1.Pin_5, IC1.GND
  N1: Part1.SCL, OLED_I2C1.SCK, M1.SCL, Mod1.SCL, A1.Pin_4
  N2: Part1.A4_I36, IC1.LO+
  N3: Part1.A3_I39, IC1.LO-
  N4: Part1.A0_DAC2, IC1.OUTPUT
  3.3V: Part1.3.3V, A1.Pin_2, IC1.3.3v
  VIN: Part1.VBUS, OLED_I2C1.VDD, M1.VIN, Mod1.VIN

custom parts:
  MakerFocus MAX30102: Oximeter module using the MAX30102 chip. As usual, if you want the mounting holes in pcb, you need to drag a hole over the pad in silkscreen to actually drill the hole (by default they are not drilled)
  gy-906: gy-906 Non-contact PIR I2C interface temperature sensor breakout board.
  ENS160 AHT21: The CO2 Gas- Air- Sensor is based on ENS160 in combination with an AHT21 Temperature Humidity Sensor.
  AD8232 HeartRate Monitor: A DIP stand-in part for whatever IC you want. With 10 pins on a 600mil dual inline package (DIP) footprint.
